# Fritzing sketch Diagrama sharp (saved by Fritzing 0.9.3b)
breadboards: 1

parts:
  J1 = Infrared Proximity Sensor
  Componente1 = Arduino Uno (Rev3)
  C1 = Electrolytic Capacitor [capacitance=1µF package="100 mil [THT, electrolytic]"]
  Componente2 = LCD1602-I2C

nets:
  N1: J1.Vout, Componente1.A0
  GND: J1.GND, Componente1.GND, C1.-, Componente2.GND
  VCC: J1.Vcc, Componente1.5V, C1.+, Componente2.VCC
  N2: Componente1.A4/SDA, Componente2.SDA
  N3: Componente1.A5/SCL, Componente2.SCL

custom parts:
  LCD1602-I2C: A standard character display, usually with 2x16 characters. Comes in many colors with LCM1602 IIC attached.
